// Logisim project ggg.circ as structural Verilog: 1 circuit, main circuit main
module main (
  input  S,
  input  A1,
  input  A0,
  input  B1,
  input  B0,
  output Y1,
  output Y0
);

  wire and_1_out, and_2_out, and_3_out, and_4_out, and_5_out, and_6_out, n3_to_8_decoder_74138_1_p4,
       n3_to_8_decoder_74138_1_p5, n3_to_8_decoder_74138_1_p6, n3_to_8_decoder_74138_1_p7,
       n3_to_8_decoder_74138_1_p8, n3_to_8_decoder_74138_2_p10, n3_to_8_decoder_74138_2_p11,
       n3_to_8_decoder_74138_2_p12, n3_to_8_decoder_74138_2_p13, n3_to_8_decoder_74138_2_p14, nand_1_out,
       nand_2_out, nand_3_out, nand_4_out, not_1_out, not_2_out, not_3_out, not_4_out, or_1_out, or_2_out,
       or_3_out, or_4_out, or_5_out, or_6_out;

  not not_1 (not_1_out, A1);
  not not_2 (not_2_out, B1);
  // _3_to_8_decoder__74138 #(.Facing("east")) 3_to_8_decoder_74138_1: pin names not known; wires that end beside it: B0, B1, A0, n3_to_8_decoder_74138_1_p4, n3_to_8_decoder_74138_1_p5, n3_to_8_decoder_74138_1_p6, n3_to_8_decoder_74138_1_p7, n3_to_8_decoder_74138_1_p8
  // _3_to_8_decoder__74138 #(.Facing("east")) 3_to_8_decoder_74138_2: pin names not known; wires that end beside it: B0, B1, A0, not_1_out, A1, 1'b0, 1'b0, 1'b0, 1'b0, n3_to_8_decoder_74138_2_p10, n3_to_8_decoder_74138_2_p11, n3_to_8_decoder_74138_2_p12, n3_to_8_decoder_74138_2_p13, n3_to_8_decoder_74138_2_p14
  and and_1 (and_1_out, not_1_out, A0);
  and and_2 (and_2_out, B0, not_2_out);
  and and_3 (and_3_out, B1, and_1_out);
  and and_4 (and_4_out, A0, B0);
  and and_5 (and_5_out, A1, and_2_out);
  or or_1 (or_1_out, and_4_out, and_5_out);
  and and_6 (and_6_out, A1, B1);
  or or_2 (or_2_out, and_3_out, or_1_out);
  nand nand_1 (nand_1_out, n3_to_8_decoder_74138_1_p5, n3_to_8_decoder_74138_1_p7);
  or or_3 (or_3_out, nand_1_out, nand_2_out);
  nand nand_2 (nand_2_out, n3_to_8_decoder_74138_2_p10, n3_to_8_decoder_74138_2_p12);
  not not_3 (not_3_out, n3_to_8_decoder_74138_2_p14);
  not not_4 (not_4_out, n3_to_8_decoder_74138_1_p4);
  nand nand_3 (nand_3_out, n3_to_8_decoder_74138_1_p6, n3_to_8_decoder_74138_1_p8);
  nand nand_4 (nand_4_out, n3_to_8_decoder_74138_2_p11, n3_to_8_decoder_74138_2_p13);
  or or_4 (or_4_out, nand_3_out, nand_4_out);
  or or_5 (or_5_out, or_3_out, not_3_out);
  or or_6 (or_6_out, not_4_out, or_4_out);
  // _4_to_1_MUX__x2___74153 #(.Facing("east")) 4_to_1_mux_x2_74153_1: pin names not known; wires that end beside it: and_6_out, or_5_out, or_2_out, or_6_out, 1'b0, S, 1'b0, S, Y1, Y0

  // Notes on the sheet:
  //   2^0 = B0
  //   A1' and A0
  //   B0 and B1'
  //   A0 and B0
  //   B1 and A1'A0
  //   A1 and B0B1'
  //   02 nand 05
  //   08 nand 11
  //   14 not
  //   01 not
  //   04 nand 07
  //   10 nand 13
  //   A1 and B1
  //   Y1
  //   Y0
  //   Y1
  //   Y0
  //   Task 1 outputs to _0, they will be active when 00
  //   Task 1 outputs to _0, they will be active when 00
  //   Task 2 outputs to _3, they will be active when 11
endmodule
